# Fritzing sketch koblingsskjema (saved by Fritzing 0.9.3b)
breadboards: 1

parts:
  Part2 = Photon
  J1 = Piezo Speaker
  R1 = Resistor [tolerance=±5% resistance=1k package=THT]
  R2 = Resistor [tolerance=±5% resistance=1k package=THT]
  LED2 = LED - 5mm [color="Red (633nm)" package="5 mm [THT]"]
  LED3 = LED - 3mm [color="Green (555nm)" package="3 mm [THT]"]
  hc-sr1 = hc-sr04
  Part1 = RFID-RC522-v3

nets:
  N1: Part2.A2, Part1.SDA
  N2: Part2.A3, Part1.SCK
  N3: Part2.A4, Part1.MISO
  N4: Part2.A5, Part1.MOSI
  GND: Part2.GND, J1.pin1, R1.Pin_0, R2.Pin_0, hc-sr1.GND, Part1.GND
  VIN: Part2.VIN, hc-sr1.VCC, Part1.3.3V
  N5: Part2.D0, LED3.anode
  N6: Part2.D1, LED2.anode
  N7: Part2.D2, Part1.RST
  N8: Part2.D3, J1.pin2
  N9: Part2.D4, hc-sr1.Trig
  N10: Part2.D5, hc-sr1.Echo
  N11: R1.Pin_1, LED2.cathode
  N12: R2.Pin_1, LED3.cathode

custom parts:
  RFID-RC522-v3: A simple China made RFID-RC522 Reader (6x4 cm); do check the pin labels, as this is a MFRC522 based clone.
